# Fritzing sketch Schema_Stampante (saved by Fritzing 0.9.3b)
breadboards: 1

parts:
  Componente4 = EasyDriver_v44
  M2 = Stepper Motor - Bipolar
  Componente5 = EasyDriver_v44
  M3 = Stepper Motor - Bipolar
  Componente6 = EasyDriver_v44
  Componente7 = EasyDriver_v44
  M4 = Stepper Motor - Bipolar
  M5 = Stepper Motor - Bipolar
  J2 = ATX24 Pin Power Supply Connector [package=atx24_right_angle]
  R1 = Temperature Sensor (Thermistor) [thermistor_type=PTC package=THT]
  R2 = Resistor [tolerance=±5% resistance=4.7k package="2512 [SMD]"]
  Q1 = Basic FET P-Channel [part_number=135N03L package="TO220 [THT]"]
  R3 = Heater
  R4 = Resistor [tolerance=±5% resistance=1k package=THT]
  J1 = STM32 Nucleo boards
  S2 = Pushbutton [package=THT]
  S3 = Pushbutton [package=THT]
  S4 = Pushbutton [package=THT]
  S5 = Pushbutton [package=THT]
  S6 = Pushbutton [package=THT]
  S7 = Pushbutton [package=THT]
  Componente8 = EasyDriver_v44
  M6 = Stepper Motor - Bipolar

nets:
  GND: Componente4.GND, Componente4.STEP, Componente4.MS1, Componente4.SLEEP, Componente4.ENABLE, Componente4.MS2, Componente5.GND, Componente5.STEP, Componente5.MS1, Componente5.SLEEP, Componente5.ENABLE, Componente5.MS2, Componente6.GND, Componente6.STEP, Componente6.MS1, Componente6.MS2, Componente7.GND, Componente7.STEP, Componente7.MS1, Componente7.MS2, J1.PB10, J1.PB5, J1.PA10, Componente8.GND, Componente8.MS1, Componente8.SLEEP, Componente8.ENABLE, Componente8.MS2
  N1: Componente4.V+, Componente5.V+, Componente6.V+, Componente7.V+, Componente8.V+
  N2: Componente4.DIR, J1.PB3
  N3: Componente4.OUT2A, M2.A
  N4: Componente4.OUT2B, M2.C
  N5: Componente4.OUT1A, M2.B
  N6: Componente4.OUT1B, M2.D
  N7: Componente5.DIR, J1.PA8
  N8: Componente5.OUT2A, M3.A
  N9: Componente5.OUT2B, M3.C
  N10: Componente5.OUT1A, M3.B
  N11: Componente5.OUT1B, M3.D
  N12: Componente6.DIR, Componente7.DIR, J1.PB4
  N13: Componente6.OUT2A, M5.A
  N14: Componente6.OUT2B, M5.C
  N15: Componente6.OUT1A, M5.B
  N16: Componente6.OUT1B, Componente6.PFD, M5.D
  N17: Componente7.OUT2A, M4.A
  N18: Componente7.OUT2B, M4.C
  N19: Componente7.OUT1A, M4.B
  N20: Componente7.OUT1B, Componente7.PFD, M4.D
  12V: J2.12V, J2.3.3V, R3.Pin_0
  N21: R1.pin_0, Q1.source
  N22: R1.pin_1, R2.Pin_0, J1.PC2
  N23: Q1.gate, R4.Pin_1
  N24: Q1.drain, R3.Pin_1
  N25: R4.Pin_0, J1.PB7
  N26: J1.D8, Componente8.STEP
  N27: J1.D9_PWM, Componente8.DIR
  N28: J1.PA0, S2.leg0
  N29: J1.PA1, S3.leg0
  N30: J1.PA4, S4.leg0
  N31: J1.PB0, S5.leg0
  N32: J1.PC1, S6.leg0
  N33: J1.PC0, S7.leg0
  N34: S2.leg1, S3.leg1, S4.leg1, S5.leg1, S6.leg1, S7.leg1
  N35: Componente8.OUT2A, M6.A
  N36: Componente8.OUT2B, M6.C
  N37: Componente8.OUT1A, M6.B
  N38: Componente8.OUT1B, M6.D

notes:
  X Axis
  Y Axis
  Z Axis
  To PC
  Heater
  GND
  NTC3950
  NC Endstops
  Ymin
  Zmin
  Xmin
  Xmax
  Zmax
  Ymax
  +6.5V
  Extruder

custom parts:
  Heater: Heater Basic schematic elements and footprints for heaters
